// Logisim project ALU.circ as structural Verilog: 1 circuit, main circuit main
module main (
  input  [15:0] rs,
  input  [15:0] rt,
  input  [2:0] shftAmnt,
  input  [2:0] ALU_Control_Input,
  output Zero,
  output [15:0] Output
);

  wire comparator_1_lt;
  wire [3:0] bit_extender_1_out;
  wire [15:0] adder_1_out, and_1_out, bit_extender_2_out, nor_1_out, or_1_out, shifter_1_out, shifter_2_out,
       subtractor_1_out;

  assign bit_extender_1_out = {{1{1'b0}}, shftAmnt};  // Bit_Extender bit_extender_1
  Adder #(.width(16)) adder_1 (.a(rs), .b(rt), .out(adder_1_out));  // open: cin, cout
  Subtractor #(.width(16)) subtractor_1 (.a(rs), .b(rt), .out(subtractor_1_out));  // open: bin, bout
  Shifter #(.width(16)) shifter_1 (.in(rs), .\dist (bit_extender_1_out), .out(shifter_1_out));
  Shifter #(.width(16), .shift("lr")) shifter_2 (.in(rs), .\dist (bit_extender_1_out), .out(shifter_2_out));
  Comparator #(.width(16)) comparator_1 (.a(rs), .b(rt), .lt(comparator_1_lt));  // open: gt, eq
  assign and_1_out = rs & rt;  // AND_Gate and_1, 16 bits wide
  assign or_1_out = rs | rt;  // OR_Gate or_1, 16 bits wide
  assign nor_1_out = ~(rs | rt);  // NOR_Gate nor_1, 16 bits wide
  assign bit_extender_2_out = {{15{1'b0}}, comparator_1_lt};  // Bit_Extender bit_extender_2
  Multiplexer #(.select(3), .width(16), .enable("false")) multiplexer_1 (
    .in0(adder_1_out), .in1(subtractor_1_out), .in2(and_1_out), .in3(or_1_out), .in4(nor_1_out),
    .in5(shifter_1_out), .in6(shifter_2_out), .in7(bit_extender_2_out), .out(Output), .sel(ALU_Control_Input));
  nor nor_2 (Zero, Output[0], Output[1], Output[2], Output[3], Output[4], Output[5], Output[6], Output[7], Output[8], Output[9], Output[10], Output[11], Output[12], Output[13], Output[14], Output[15]);

  // Notes on the sheet:
  //   ALU
endmodule
