// Logisim project ALUControl.circ as structural Verilog: 1 circuit, main circuit main
module main (
  input  [3:0] Opcode,
  input  [1:0] ALUOP,
  output [2:0] ALUControl_Input
);

  wire and_1_out, or_1_out;

  and and_1 (and_1_out, Opcode[0], ALUOP[1]);
  or or_1 (or_1_out, Opcode[2], Opcode[1]);
  and and_2 (ALUControl_Input[2], Opcode[2], ALUOP[1]);
  or or_2 (ALUControl_Input[0], and_1_out, ALUOP[0]);
  and and_3 (ALUControl_Input[1], ALUOP[1], or_1_out);
endmodule
