// Logisim project Control.circ as structural Verilog: 1 circuit, main circuit main
module main (
  input  [3:0] Opcode,
  input  [2:0] shftAmnt,
  output RegDst,
  output ALUSrc,
  output MemtoReg,
  output RegWrite,
  output bne,
  output MemRead,
  output MemWrite,
  output beq,
  output ALUOP0,
  output ALUOP1
);

  wire addi_out, andi_out, ori_out;

  nor nor_1 (RegDst, shftAmnt[0], shftAmnt[1], shftAmnt[2]);
  and lw (MemRead, ~Opcode[0], Opcode[1], ~Opcode[2], Opcode[3]);  // AND_Gate
  and sw (MemWrite, Opcode[0], Opcode[1], ~Opcode[2], Opcode[3]);  // AND_Gate
  and u_beq (beq, ~Opcode[0], Opcode[1], Opcode[2], Opcode[3]);  // AND_Gate
  and u_bne (bne, Opcode[0], Opcode[1], Opcode[2], Opcode[3]);
  and addi (addi_out, Opcode[0], ~Opcode[1], ~Opcode[2], Opcode[3]);  // AND_Gate
  and andi (andi_out, ~Opcode[0], ~Opcode[1], Opcode[2], Opcode[3]);  // AND_Gate
  and ori (ori_out, Opcode[0], ~Opcode[1], Opcode[2], Opcode[3]);  // AND_Gate
  or or_1 (ALUOP0, ori_out, andi_out, addi_out, bne, beq);
  or or_2 (ALUOP1, ori_out, andi_out, addi_out, RegDst);
  or or_3 (ALUSrc, MemRead, ori_out, andi_out, addi_out, MemWrite);
  or or_4 (RegWrite, RegDst, ori_out, andi_out, addi_out, MemRead);

  assign MemtoReg = MemRead;
endmodule
