// Logisim project Datapath.circ as structural Verilog: 1 circuit, main circuit main
module main (
  input  in_1,
  output [15:0] out_2,
  output [2:0] out_3,
  output [2:0] out_4,
  output [15:0] out_5,
  output [2:0] out_6,
  output [15:0] out_7,
  output out_8,
  output [3:0] out_9
);

  wire Alusrc, and_1_out, and_2_out, beq, bne, clk, memRd, memtoReg, memWrt, PCSrc, regWrt, zero;
  wire [1:0] Aluop;
  wire [2:0] main_4_alucontrol_input, multiplexer_1_out;
  wire [15:0] adder_1_out, adder_2_out, bit_extender_1_out, main_3_output, multiplexer_2_out,
       multiplexer_3_out, multiplexer_4_out, ram_1_data, register_1_q;

  Clock clock_1 (.out(clk));
  Control_main main_1 (
    .Opcode(out_5[15:12]), .shftAmnt(out_5[2:0]), .RegDst(out_8), .ALUSrc(Alusrc), .MemtoReg(memtoReg),
    .RegWrite(regWrt), .bne(bne), .MemRead(memRd), .MemWrite(memWrt), .beq(beq), .ALUOP0(Aluop[0]),
    .ALUOP1(Aluop[1]));
  Register #(.width(16)) register_1 (.D(multiplexer_3_out), .Q(register_1_q), .clk(clk), .clr(in_1));  // open: en
  Adder #(.width(16)) adder_1 (.a(16'h1), .b(register_1_q), .out(adder_1_out));  // open: cin, cout
  ROM #(.addrWidth(16), .dataWidth(16)) rom_1 (
    .addr(register_1_q), .data({out_5[15:12], out_3, out_4, out_5[5:0]}));  // open: sel
  Multiplexer #(.width(3), .enable("false")) multiplexer_1 (
    .in0(out_4), .in1(out_5[5:3]), .out(multiplexer_1_out), .sel(out_8));
  assign bit_extender_1_out = {{10{1'b0}}, out_5[5:0]};  // Bit_Extender bit_extender_1
  REG_main main_2 (
    .data(multiplexer_4_out), .Read1(out_3), .wrtAdrs(multiplexer_1_out), .Read2(out_4), .clk(clk),
    .out_7(out_2), .out_8(out_7), .regWrt(regWrt));
  Adder #(.width(16)) adder_2 (.a(adder_1_out), .b(bit_extender_1_out), .out(adder_2_out));  // open: cin, cout
  Multiplexer #(.width(16), .enable("false")) multiplexer_2 (
    .in0(out_7), .in1(bit_extender_1_out), .out(multiplexer_2_out), .sel(Alusrc));
  and and_1 (and_1_out, zero, beq);
  and and_2 (and_2_out, ~zero, bne);  // AND_Gate
  Multiplexer #(.width(16), .enable("false")) multiplexer_3 (
    .in0(adder_1_out), .in1(adder_2_out), .out(multiplexer_3_out), .sel(PCSrc));
  ALU_main main_3 (
    .rs(out_2), .rt(multiplexer_2_out), .shftAmnt(out_5[2:0]), .Zero(zero), .Output(main_3_output),
    .ALU_Control_Input(main_4_alucontrol_input));
  ALUControl_main main_4 (.Opcode(out_5[15:12]), .ALUOP(Aluop), .ALUControl_Input(main_4_alucontrol_input));
  or or_1 (PCSrc, and_1_out, and_2_out);
  Multiplexer #(.width(16), .enable("false")) multiplexer_4 (
    .in0(main_3_output), .in1(ram_1_data), .out(multiplexer_4_out), .sel(memtoReg));
  RAM #(.addrWidth(16), .dataWidth(16), .bus("separate")) ram_1 (
    .addr(main_3_output), .din(out_7), .data(ram_1_data), .str(memWrt), .clk(clk), .ld(memRd));  // open: sel, clr

  assign out_5[11:6] = {out_3, out_4};
  assign out_6 = out_5[2:0];
  assign out_9 = out_5[15:12];

  // Other names for the same wires on the sheet: shmt[2:0] = out_5[2:0]; rd[2:0] = out_5[5:3]; rt[2:0] = out_4;
  //   rs[2:0] = out_3; Opcode[3:0] = out_5[15:12]; regDst = out_8

  // Notes on the sheet:
  //   contents of rom_1 (hex, n*v repeats v):
  //   8743 1100 1010 1111
endmodule
