// Logisim project REG.circ as structural Verilog: 1 circuit, main circuit main
module main (
  input  [15:0] data,
  input  [2:0] Read1,
  input  [2:0] wrtAdrs,
  input  [2:0] Read2,
  input  clk,
  input  regWrt,
  output [15:0] out_7,
  output [15:0] out_8
);

  wire and_1_out, and_2_out, and_3_out, and_4_out, and_5_out, and_6_out, and_7_out, and_8_out,
       decoder_1_out0, decoder_1_out1, decoder_1_out2, decoder_1_out3, decoder_1_out4, decoder_1_out5,
       decoder_1_out6, decoder_1_out7;
  wire [15:0] register_1_q, register_2_q, register_3_q, register_4_q, register_5_q, register_6_q,
       register_7_q, register_8_q;

  Decoder #(.select(3), .disabled(0)) decoder_1 (
    .out0(decoder_1_out0), .out1(decoder_1_out1), .out2(decoder_1_out2), .out3(decoder_1_out3),
    .out4(decoder_1_out4), .out5(decoder_1_out5), .out6(decoder_1_out6), .out7(decoder_1_out7), .sel(wrtAdrs));  // open: en
  and and_1 (and_1_out, decoder_1_out0, regWrt);
  and and_2 (and_2_out, decoder_1_out1, regWrt);
  and and_3 (and_3_out, decoder_1_out2, regWrt);
  and and_4 (and_4_out, decoder_1_out3, regWrt);
  and and_5 (and_5_out, decoder_1_out4, regWrt);
  and and_6 (and_6_out, decoder_1_out5, regWrt);
  and and_7 (and_7_out, decoder_1_out6, regWrt);
  and and_8 (and_8_out, decoder_1_out7, regWrt);
  Register #(.width(16)) register_1 (.D(data), .en(and_1_out), .Q(register_1_q), .clk(clk));  // open: clr
  Register #(.width(16)) register_2 (.D(data), .en(and_2_out), .Q(register_2_q), .clk(clk));  // open: clr
  Register #(.width(16)) register_3 (.D(data), .en(and_3_out), .Q(register_3_q), .clk(clk));  // open: clr
  Register #(.width(16)) register_4 (.D(data), .en(and_4_out), .Q(register_4_q), .clk(clk));  // open: clr
  Register #(.width(16)) register_5 (.D(data), .en(and_5_out), .Q(register_5_q), .clk(clk));  // open: clr
  Register #(.width(16)) register_6 (.D(data), .en(and_6_out), .Q(register_6_q), .clk(clk));  // open: clr
  Register #(.width(16)) register_7 (.D(data), .en(and_7_out), .Q(register_7_q), .clk(clk));  // open: clr
  Register #(.width(16)) register_8 (.D(data), .en(and_8_out), .Q(register_8_q), .clk(clk));  // open: clr
  Multiplexer #(.select(3), .width(16)) multiplexer_1 (
    .in0(register_1_q), .in1(register_2_q), .in2(register_3_q), .in3(register_4_q), .in4(register_5_q),
    .in5(register_6_q), .in6(register_7_q), .in7(register_8_q), .out(out_7), .sel(Read1));  // open: en
  Multiplexer #(.select(3), .width(16)) multiplexer_2 (
    .in0(register_1_q), .in1(register_2_q), .in2(register_3_q), .in3(register_4_q), .in4(register_5_q),
    .in5(register_6_q), .in6(register_7_q), .in7(register_8_q), .out(out_8), .sel(Read2));  // open: en

  // Notes on the sheet:
  //   Registar
endmodule
